# Fritzing sketch Circuit (saved by Fritzing 0.9.5d)
breadboards: 1

parts:
  M1 = DOIT Esp32 DevKit v1 (30 pins long, 11 pins width) [part_number=ESP32S-PIN30]
  Part1 = BME280 Breakout
  Capacitive_Soil_Moisture_Sensor1 = DFRobot Capacitive Soil Moisture Sensor V1.0 [part_number=SEN0193]
  J1 = female pin header, 4 pins [form="♀ (female)"]
  RS485_module1 = RS485 Module (MAX3485)
  Part2 = Jtron 1 Channel Optoisolated Relay Module [package=relay]
  Part4 = Jtron 1 Channel Optoisolated Relay Module [package=relay]
  Part3 = Jtron 1 Channel Optoisolated Relay Module [package=relay]

nets:
  VCC: M1.3V3, Part1.3.3V, Capacitive_Soil_Moisture_Sensor1.VCC, RS485_module1.VCC
  GND: M1.GND, Part1.GND, Capacitive_Soil_Moisture_Sensor1.GND, RS485_module1.GND, Part2.GND, Part4.GND, Part3.GND
  N1: M1.RX2, RS485_module1.DI
  N2: M1.TX2, RS485_module1.RO
  N3: M1.D21, Part1.SDI/SDA
  N4: M1.D22, Part1.SCK/SCL
  N5: M1.D34, Capacitive_Soil_Moisture_Sensor1.A
  N6: M1.D33, Part4.IN1
  N7: M1.D25, Part3.IN1
  N8: M1.D26, Part2.IN1
  N9: M1.D14, RS485_module1.RE
  N10: M1.D12, RS485_module1.DE
  VCC_2: M1.VIN, Part2.VCC, Part4.VCC, Part3.VCC
  N11: J1.pin2, RS485_module1.A
  N12: J1.pin3, RS485_module1.B

notes:
  9V 5A Adapter

custom parts:
  DOIT Esp32 DevKit v1 (30 pins long, 11 pins width): The DOIT Esp32 DevKit v1 is one of the development board created by DOIT to evaluate the ESP-WROOM-32 module. It is based on the ESP32 microcontroller that boasts Wifi, Bluetooth, Ethernet and Low Power support all in a single chip. (vanepp) made breadboard work, adjusted pin numbering and labels and reduced size of schematic and cleaned up pcb. This chip is 30pins long (2 x15) and 11 pins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
  DFRobot Capacitive Soil Moisture Sensor V1.0: DFRobot Capacitive Soil Moisture Sensor V1.0 This product measures soil moisture levels by capacitive sensing, rather than resistive sensing like other types of moisture sensor. It is made of a corrosion resistant material giving it a long service life. Insert it into soil and impress your friends with the real-time soil moisture data! The product includes an on-board voltage regulator which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
  RS485 Module (MAX3485): Commercially available RS485 to RS232 TTL Module
